// Logisim project tetris.circ as structural Verilog: 12 circuits, main circuit tetris
module tetris (
  input  FALL
);

  wire and_1_out, and_2_out, button_1_out, button_2_out, button_3_out, clock_1_out, clock_2_out, clock_3_out,
       clock_4_out, clock_5_out, clock_6_out, COLLISION, comparator_1_eq, comparator_2_eq, comparator_3_eq,
       comparator_4_eq, comparator_5_eq, comparator_6_eq, comparator_7_eq, comparator_8_eq, comparator_9_eq,
       comparator_10_eq, comparator_11_eq, comparator_12_eq, d_ff_1_q, d_ff_2_q, FLIP, LEFT, or_11_out, RIGHT;
  wire [3:0] adder_1_out, block_addr_gen_1_out_addr_low_4, disp_address_gen_1__0, disp_address_gen_1__1,
       disp_address_gen_1__2, disp_address_gen_1__3, disp_address_gen_1__4, disp_address_gen_1__5,
       disp_address_gen_1__6, disp_address_gen_1__7, disp_address_gen_1__8, disp_address_gen_1__9;
  wire [4:0] auto_fall_1_out, move_1_out, register_1_q, register_22_q, subtractor_1_out, subtractor_2_out,
       subtractor_3_out, subtractor_4_out;
  wire [5:0] flip_logic_1_out, gen_rand_block_1_block_num;
  wire [9:0] block_addr_gen_1_out_addr;
  wire [19:0] multiplexer_1_out, NEW_MAP0, NEW_MAP1, NEW_MAP2, NEW_MAP3, NEW_MAP4, NEW_MAP5, NEW_MAP6,
       NEW_MAP7, NEW_MAP8, NEW_MAP9, OLD_MAP0, OLD_MAP1, OLD_MAP2, OLD_MAP3, OLD_MAP4, OLD_MAP5, OLD_MAP6,
       OLD_MAP7, OLD_MAP8, OLD_MAP9, or_1_out, or_2_out, or_3_out, or_4_out, or_5_out, or_6_out, or_7_out,
       or_8_out, or_9_out, or_10_out, or_12_out, or_13_out, or_14_out, or_15_out, or_16_out, or_17_out,
       or_18_out, or_19_out, or_20_out, or_21_out, register_2_q, register_3_q, register_4_q, register_5_q,
       register_6_q, register_7_q, register_8_q, register_9_q, register_10_q, register_11_q, register_23_q,
       register_24_q, register_25_q, register_26_q, register_27_q, register_28_q, register_29_q,
       register_30_q, register_31_q, register_32_q, rom_1_data, row_detect_1_out_13, row_detect_1_out_14,
       row_detect_1_out_15, row_detect_1_out_16, row_detect_1_out_17, row_detect_1_out_18,
       row_detect_1_out_19, row_detect_1_out_20, row_detect_1_out_21, row_detect_1_out_22,
       row_detect_2_out_13, row_detect_2_out_14, row_detect_2_out_15, row_detect_2_out_16,
       row_detect_2_out_17, row_detect_2_out_18, row_detect_2_out_19, row_detect_2_out_20,
       row_detect_2_out_21, row_detect_2_out_22, row_detect_3_out_13, row_detect_3_out_14,
       row_detect_3_out_15, row_detect_3_out_16, row_detect_3_out_17, row_detect_3_out_18,
       row_detect_3_out_19, row_detect_3_out_20, row_detect_3_out_21, row_detect_3_out_22, shifter_1_out;

  gen_rand_block gen_rand_block_1 (.NEXT(and_2_out), .BLOCK_NUM(gen_rand_block_1_block_num));
  flip_logic flip_logic_1 (.BLOCK_NUM(gen_rand_block_1_block_num), .FLIP(FLIP), .OUT(flip_logic_1_out));
  Comparator #(.width(4), .mode("unsigned")) comparator_1 (
    .a(block_addr_gen_1_out_addr_low_4), .b(4'b1100), .eq(comparator_1_eq));  // open: gt, lt
  move move_1 (.CURR_POS(register_1_q), .in_2(LEFT), .OUT(move_1_out), .in_3(RIGHT));  // open: carry
  block_addr_gen block_addr_gen_1 (
    .BLOCK_NUM(flip_logic_1_out), .OUT_ADDR(block_addr_gen_1_out_addr),
    .OUT_ADDR_LOW_4(block_addr_gen_1_out_addr_low_4));
  and and_1 (and_1_out, comparator_1_eq, and_2_out);
  Subtractor #(.width(5)) subtractor_1 (.a(5'b01010), .b(register_1_q), .out(subtractor_1_out));  // open: bin, bout
  disp_address_gen disp_address_gen_1 (
    ._0(disp_address_gen_1__0), ._1(disp_address_gen_1__1), ._2(disp_address_gen_1__2),
    ._3(disp_address_gen_1__3), ._4(disp_address_gen_1__4), ._5(disp_address_gen_1__5),
    ._6(disp_address_gen_1__6), ._7(disp_address_gen_1__7), ._8(disp_address_gen_1__8),
    ._9(disp_address_gen_1__9), .Y(subtractor_1_out));
  Register #(.width(5)) register_1 (.D(move_1_out), .Q(register_1_q), .clk(clock_1_out), .clr(and_2_out));  // open: en
  Clock clock_1 (.out(clock_1_out));
  auto_fall auto_fall_1 (.SPEED(8'h2f), .FALL(FALL), .OUT(auto_fall_1_out), .RESET(and_1_out));
  ROM #(.addrWidth(10), .dataWidth(20)) rom_1 (.addr(block_addr_gen_1_out_addr), .data(rom_1_data));  // open: sel
  Shifter #(.width(20), .shift("lr")) shifter_1 (.in(rom_1_data), .\dist (auto_fall_1_out), .out(shifter_1_out));
  Register #(.width(20)) register_2 (
    .D(shifter_1_out), .en(comparator_2_eq), .Q(register_2_q), .clk(clock_2_out));  // open: clr
  Comparator #(.width(4), .mode("unsigned")) comparator_2 (
    .a(block_addr_gen_1_out_addr_low_4), .b(disp_address_gen_1__0), .eq(comparator_2_eq));  // open: gt, lt
  Register #(.width(20)) register_3 (
    .D(shifter_1_out), .en(comparator_3_eq), .Q(register_3_q), .clk(clock_2_out));  // open: clr
  Comparator #(.width(4), .mode("unsigned")) comparator_3 (
    .a(block_addr_gen_1_out_addr_low_4), .b(disp_address_gen_1__1), .eq(comparator_3_eq));  // open: gt, lt
  Register #(.width(20)) register_4 (
    .D(shifter_1_out), .en(comparator_4_eq), .Q(register_4_q), .clk(clock_2_out));  // open: clr
  Comparator #(.width(4), .mode("unsigned")) comparator_4 (
    .a(block_addr_gen_1_out_addr_low_4), .b(disp_address_gen_1__2), .eq(comparator_4_eq));  // open: gt, lt
  Register #(.width(20)) register_5 (
    .D(shifter_1_out), .en(comparator_5_eq), .Q(register_5_q), .clk(clock_2_out));  // open: clr
  Comparator #(.width(4), .mode("unsigned")) comparator_5 (
    .a(block_addr_gen_1_out_addr_low_4), .b(disp_address_gen_1__3), .eq(comparator_5_eq));  // open: gt, lt
  Register #(.width(20)) register_6 (
    .D(shifter_1_out), .en(comparator_6_eq), .Q(register_6_q), .clk(clock_2_out));  // open: clr
  Comparator #(.width(4), .mode("unsigned")) comparator_6 (
    .a(block_addr_gen_1_out_addr_low_4), .b(disp_address_gen_1__4), .eq(comparator_6_eq));  // open: gt, lt
  Register #(.width(20)) register_7 (
    .D(shifter_1_out), .en(comparator_7_eq), .Q(register_7_q), .clk(clock_2_out));  // open: clr
  Comparator #(.width(4), .mode("unsigned")) comparator_7 (
    .a(block_addr_gen_1_out_addr_low_4), .b(disp_address_gen_1__5), .eq(comparator_7_eq));  // open: gt, lt
  Register #(.width(20)) register_8 (
    .D(shifter_1_out), .en(comparator_8_eq), .Q(register_8_q), .clk(clock_2_out));  // open: clr
  Comparator #(.width(4), .mode("unsigned")) comparator_8 (
    .a(block_addr_gen_1_out_addr_low_4), .b(disp_address_gen_1__6), .eq(comparator_8_eq));  // open: gt, lt
  Register #(.width(20)) register_9 (
    .D(shifter_1_out), .en(comparator_9_eq), .Q(register_9_q), .clk(clock_2_out));  // open: clr
  Comparator #(.width(4), .mode("unsigned")) comparator_9 (
    .a(block_addr_gen_1_out_addr_low_4), .b(disp_address_gen_1__7), .eq(comparator_9_eq));  // open: gt, lt
  Register #(.width(20)) register_10 (
    .D(shifter_1_out), .en(comparator_10_eq), .Q(register_10_q), .clk(clock_2_out));  // open: clr
  Comparator #(.width(4), .mode("unsigned")) comparator_10 (
    .a(block_addr_gen_1_out_addr_low_4), .b(disp_address_gen_1__8), .eq(comparator_10_eq));  // open: gt, lt
  Register #(.width(20)) register_11 (
    .D(shifter_1_out), .en(comparator_11_eq), .Q(register_11_q), .clk(clock_2_out));  // open: clr
  Comparator #(.width(4), .mode("unsigned")) comparator_11 (
    .a(block_addr_gen_1_out_addr_low_4), .b(disp_address_gen_1__9), .eq(comparator_11_eq));  // open: gt, lt
  Clock clock_2 (.out(clock_2_out));
  Comparator #(.width(4), .mode("unsigned")) comparator_12 (
    .a(block_addr_gen_1_out_addr_low_4), .b(4'b1011), .eq(comparator_12_eq));  // open: gt, lt
  Adder #(.width(4)) adder_1 (
    .a(block_addr_gen_1_out_addr_low_4), .b(register_1_q[3:0]), .out(adder_1_out));  // open: cin, cout
  Clock clock_3 (.out(clock_3_out));
  D_Flip_Flop d_ff_1 (.clk(clock_3_out), .D(and_2_out), .Q(d_ff_1_q));  // open: Qn, preset, en, reset
  and and_2 (and_2_out, comparator_12_eq, COLLISION);
  D_Flip_Flop d_ff_2 (.clk(clock_3_out), .D(d_ff_1_q), .Q(d_ff_2_q));  // open: Qn, preset, en, reset
  assign or_1_out = NEW_MAP0 | register_2_q;  // OR_Gate or_1, 20 bits wide
  assign or_2_out = NEW_MAP1 | register_3_q;  // OR_Gate or_2, 20 bits wide
  assign or_3_out = NEW_MAP2 | register_4_q;  // OR_Gate or_3, 20 bits wide
  assign or_4_out = NEW_MAP3 | register_5_q;  // OR_Gate or_4, 20 bits wide
  assign or_5_out = NEW_MAP4 | register_6_q;  // OR_Gate or_5, 20 bits wide
  assign or_6_out = NEW_MAP5 | register_7_q;  // OR_Gate or_6, 20 bits wide
  assign or_7_out = NEW_MAP6 | register_8_q;  // OR_Gate or_7, 20 bits wide
  assign or_8_out = NEW_MAP7 | register_9_q;  // OR_Gate or_8, 20 bits wide
  assign or_9_out = NEW_MAP8 | register_10_q;  // OR_Gate or_9, 20 bits wide
  assign or_10_out = NEW_MAP9 | register_11_q;  // OR_Gate or_10, 20 bits wide
  or or_11 (or_11_out, and_2_out, d_ff_2_q);
  Register #(.width(20)) register_12 (.D(or_1_out), .en(or_11_out), .Q(OLD_MAP0), .clk(clock_4_out));  // open: clr
  Register #(.width(20)) register_13 (.D(or_2_out), .en(or_11_out), .Q(OLD_MAP1), .clk(clock_4_out));  // open: clr
  Register #(.width(20)) register_14 (.D(or_3_out), .en(or_11_out), .Q(OLD_MAP2), .clk(clock_4_out));  // open: clr
  Register #(.width(20)) register_15 (.D(or_4_out), .en(or_11_out), .Q(OLD_MAP3), .clk(clock_4_out));  // open: clr
  Register #(.width(20)) register_16 (.D(or_5_out), .en(or_11_out), .Q(OLD_MAP4), .clk(clock_4_out));  // open: clr
  Register #(.width(20)) register_17 (.D(or_6_out), .en(or_11_out), .Q(OLD_MAP5), .clk(clock_4_out));  // open: clr
  Register #(.width(20)) register_18 (.D(or_7_out), .en(or_11_out), .Q(OLD_MAP6), .clk(clock_4_out));  // open: clr
  Register #(.width(20)) register_19 (.D(or_8_out), .en(or_11_out), .Q(OLD_MAP7), .clk(clock_4_out));  // open: clr
  Register #(.width(20)) register_20 (.D(or_9_out), .en(or_11_out), .Q(OLD_MAP8), .clk(clock_4_out));  // open: clr
  Register #(.width(20)) register_21 (.D(or_10_out), .en(or_11_out), .Q(OLD_MAP9), .clk(clock_4_out));  // open: clr
  Clock clock_4 (.out(clock_4_out));
  Register #(.width(5)) register_22 (
    .D(auto_fall_1_out), .en(COLLISION), .Q(register_22_q), .clk(clock_5_out));  // open: clr
  Clock clock_5 (.out(clock_5_out));
  Multiplexer #(.select(4), .width(20)) multiplexer_1 (
    .in0(OLD_MAP0), .in1(OLD_MAP1), .in2(OLD_MAP2), .in3(OLD_MAP3), .in4(OLD_MAP4), .in5(OLD_MAP5),
    .in6(OLD_MAP6), .in7(OLD_MAP7), .in8(OLD_MAP8), .in9(OLD_MAP9), .in10({20{1'b0}}), .in11({20{1'b0}}),
    .in12({20{1'b0}}), .in13({20{1'b0}}), .in14({20{1'b0}}), .in15({20{1'b0}}), .out(multiplexer_1_out),
    .sel(adder_1_out));  // open: en
  row_detect row_detect_1 (
    ._0(OLD_MAP0), ._1(OLD_MAP1), ._2(OLD_MAP2), ._3(OLD_MAP3), ._4(OLD_MAP4), ._5(OLD_MAP5), ._6(OLD_MAP6),
    ._7(OLD_MAP7), ._8(OLD_MAP8), ._9(OLD_MAP9), .ROW(register_22_q), .out_13(row_detect_1_out_13),
    .out_14(row_detect_1_out_14), .out_15(row_detect_1_out_15), .out_16(row_detect_1_out_16),
    .out_17(row_detect_1_out_17), .out_18(row_detect_1_out_18), .out_19(row_detect_1_out_19),
    .out_20(row_detect_1_out_20), .out_21(row_detect_1_out_21), .out_22(row_detect_1_out_22));  // open: HIT
  assign or_12_out = register_2_q | OLD_MAP0;  // OR_Gate or_12, 20 bits wide
  assign or_13_out = register_3_q | OLD_MAP1;  // OR_Gate or_13, 20 bits wide
  assign or_14_out = register_4_q | OLD_MAP2;  // OR_Gate or_14, 20 bits wide
  assign or_15_out = register_5_q | OLD_MAP3;  // OR_Gate or_15, 20 bits wide
  assign or_16_out = register_6_q | OLD_MAP4;  // OR_Gate or_16, 20 bits wide
  assign or_17_out = register_7_q | OLD_MAP5;  // OR_Gate or_17, 20 bits wide
  assign or_18_out = register_8_q | OLD_MAP6;  // OR_Gate or_18, 20 bits wide
  assign or_19_out = register_9_q | OLD_MAP7;  // OR_Gate or_19, 20 bits wide
  assign or_20_out = register_10_q | OLD_MAP8;  // OR_Gate or_20, 20 bits wide
  assign or_21_out = register_11_q | OLD_MAP9;  // OR_Gate or_21, 20 bits wide
  Clock #(.highDuration(16), .lowDuration(16)) clock_6 (.out(clock_6_out));
  DotMatrix #(.matrixcols(10), .matrixrows(20)) dotmatrix_1 (
    .col0(register_23_q), .col1(register_24_q), .col2(register_25_q), .col3(register_26_q),
    .col4(register_27_q), .col5(register_28_q), .col6(register_29_q), .col7(register_30_q),
    .col8(register_31_q), .col9(register_32_q));
  Register #(.width(20)) register_23 (.D(or_12_out), .Q(register_23_q), .clk(clock_6_out));  // open: en, clr
  Register #(.width(20)) register_24 (.D(or_13_out), .Q(register_24_q), .clk(clock_6_out));  // open: en, clr
  Register #(.width(20)) register_25 (.D(or_14_out), .Q(register_25_q), .clk(clock_6_out));  // open: en, clr
  Register #(.width(20)) register_26 (.D(or_15_out), .Q(register_26_q), .clk(clock_6_out));  // open: en, clr
  Register #(.width(20)) register_27 (.D(or_16_out), .Q(register_27_q), .clk(clock_6_out));  // open: en, clr
  Register #(.width(20)) register_28 (.D(or_17_out), .Q(register_28_q), .clk(clock_6_out));  // open: en, clr
  Register #(.width(20)) register_29 (.D(or_18_out), .Q(register_29_q), .clk(clock_6_out));  // open: en, clr
  Register #(.width(20)) register_30 (.D(or_19_out), .Q(register_30_q), .clk(clock_6_out));  // open: en, clr
  Register #(.width(20)) register_31 (.D(or_20_out), .Q(register_31_q), .clk(clock_6_out));  // open: en, clr
  Register #(.width(20)) register_32 (.D(or_21_out), .Q(register_32_q), .clk(clock_6_out));  // open: en, clr
  collision_detect collision_detect_1 (
    .BLOCK(shifter_1_out), .MAP(multiplexer_1_out), .ACK(and_2_out), .COLLISION(COLLISION));
  Subtractor #(.width(5)) subtractor_2 (.a(5'b10011), .b(register_22_q), .out(subtractor_2_out));  // open: bin, bout
  row_detect row_detect_2 (
    ._0(row_detect_1_out_13), ._1(row_detect_1_out_14), ._2(row_detect_1_out_15), ._3(row_detect_1_out_16),
    ._4(row_detect_1_out_17), ._5(row_detect_1_out_18), ._6(row_detect_1_out_19), ._7(row_detect_1_out_20),
    ._8(row_detect_1_out_21), ._9(row_detect_1_out_22), .ROW(subtractor_2_out), .out_13(row_detect_2_out_13),
    .out_14(row_detect_2_out_14), .out_15(row_detect_2_out_15), .out_16(row_detect_2_out_16),
    .out_17(row_detect_2_out_17), .out_18(row_detect_2_out_18), .out_19(row_detect_2_out_19),
    .out_20(row_detect_2_out_20), .out_21(row_detect_2_out_21), .out_22(row_detect_2_out_22));  // open: HIT
  Subtractor #(.width(5)) subtractor_3 (.a(5'b10010), .b(register_22_q), .out(subtractor_3_out));  // open: bin, bout
  row_detect row_detect_3 (
    ._0(row_detect_2_out_13), ._1(row_detect_2_out_14), ._2(row_detect_2_out_15), ._3(row_detect_2_out_16),
    ._4(row_detect_2_out_17), ._5(row_detect_2_out_18), ._6(row_detect_2_out_19), ._7(row_detect_2_out_20),
    ._8(row_detect_2_out_21), ._9(row_detect_2_out_22), .ROW(subtractor_3_out), .out_13(row_detect_3_out_13),
    .out_14(row_detect_3_out_14), .out_15(row_detect_3_out_15), .out_16(row_detect_3_out_16),
    .out_17(row_detect_3_out_17), .out_18(row_detect_3_out_18), .out_19(row_detect_3_out_19),
    .out_20(row_detect_3_out_20), .out_21(row_detect_3_out_21), .out_22(row_detect_3_out_22));  // open: HIT
  Button button_1 (.out(button_1_out));
  Button button_2 (.out(button_2_out));
  diff diff_1 (.in(button_2_out), .out(LEFT));
  diff diff_2 (.in(button_1_out), .out(FLIP));
  Button button_3 (.out(button_3_out));
  diff diff_3 (.in(button_3_out), .out(RIGHT));
  Subtractor #(.width(5)) subtractor_4 (.a(5'b10001), .b(register_22_q), .out(subtractor_4_out));  // open: bin, bout
  row_detect row_detect_4 (
    ._0(row_detect_3_out_13), ._1(row_detect_3_out_14), ._2(row_detect_3_out_15), ._3(row_detect_3_out_16),
    ._4(row_detect_3_out_17), ._5(row_detect_3_out_18), ._6(row_detect_3_out_19), ._7(row_detect_3_out_20),
    ._8(row_detect_3_out_21), ._9(row_detect_3_out_22), .ROW(subtractor_4_out), .out_13(NEW_MAP0),
    .out_14(NEW_MAP1), .out_15(NEW_MAP2), .out_16(NEW_MAP3), .out_17(NEW_MAP4), .out_18(NEW_MAP5),
    .out_19(NEW_MAP6), .out_20(NEW_MAP7), .out_21(NEW_MAP8), .out_22(NEW_MAP9));  // open: HIT

  // Notes on the sheet:
  //   contents of rom_1 (hex, n*v repeats v):
  //   80000 c0000 80000 13*0 40000 e0000 14*0 40000 c0000 40000 13*0 e0000 40000 14*0 e0000 80000 14*0
  //   80000 80000 c0000 13*0 20000 e0000 14*0 c0000 40000 40000 13*0 80000 e0000 14*0 40000 40000 c0000
  //   13*0 e0000 20000 14*0 c0000 80000 80000 13*0 c0000 c0000 14*0 f0000 15*0 4*80000 12*0 c0000 60000
  //   14*0 40000 c0000 80000 13*0 60000 c0000 14*0 80000 c0000 40000 15*0 1f80 400 1f80 0 0 1f80
  //   LEFT
  //   FLIP
  //   RIGHT
endmodule

module move (
  input  [4:0] CURR_POS,
  input  in_2,
  input  in_3,
  output [4:0] OUT,
  output carry
);

  wire subtractor_1_bout;
  wire [4:0] adder_1_out, subtractor_1_out;

  Adder #(.width(5)) adder_1 (.a(CURR_POS), .b(5'b00001), .out(adder_1_out), .cin(1'b0));  // open: cout
  Subtractor #(.width(5)) subtractor_1 (
    .a(CURR_POS), .b(5'b00001), .out(subtractor_1_out), .bin(1'b0), .bout(subtractor_1_bout));
  Multiplexer #(.select(2), .width(5), .enable("false")) multiplexer_1 (
    .in0(CURR_POS), .in1(adder_1_out), .in2(subtractor_1_out), .in3(CURR_POS), .out(OUT), .sel({in_2, in_3}));
  and and_1 (carry, in_2, subtractor_1_bout);
endmodule

module diff (
  input  in,
  output out
);

  wire and_1_out, clock_1_out, d_ff_1_q, not_1_out;

  Clock clock_1 (.out(clock_1_out));
  D_Flip_Flop d_ff_1 (.clk(clock_1_out), .D(in), .Q(d_ff_1_q), .en(clock_1_out));  // open: Qn, preset, reset
  not not_1 (not_1_out, d_ff_1_q);
  and and_1 (and_1_out, in, not_1_out);
  D_Flip_Flop d_ff_2 (.clk(clock_1_out), .D(and_1_out), .Q(out));  // open: Qn, preset, en, reset
endmodule

module disp_address_gen (
  input  [4:0] Y,
  output [3:0] _0,
  output [3:0] _1,
  output [3:0] _2,
  output [3:0] _3,
  output [3:0] _4,
  output [3:0] _5,
  output [3:0] _6,
  output [3:0] _7,
  output [3:0] _8,
  output [3:0] _9
);

  wire [3:0] undriven, undriven_2, undriven_3, undriven_4, undriven_5, undriven_6, undriven_7, undriven_8,
       undriven_9, undriven_10;
  wire [4:0] adder_1_out, adder_2_out, adder_3_out, adder_4_out, adder_5_out, adder_6_out, adder_7_out,
       adder_8_out, adder_9_out;

  Multiplexer #(.select(5), .width(4)) multiplexer_1 (
    .in0(4'b0000), .in1(4'b0001), .in2(4'b0010), .in3(4'b0011), .in4(4'b0100), .in5(4'b0101), .in6(4'b0110),
    .in7(4'b0111), .in8(4'b1000), .in9(4'b1001), .in10(4'b0000), .in11(4'b0001), .in12(4'b0010),
    .in13(4'b0011), .in14(4'b0100), .in15(4'b0101), .in16(4'b0110), .in17(4'b0111), .in18(4'b1000),
    .in19(4'b1001), .in20(4'b0000), .in21(4'b0001), .in22(4'b0010), .in23(4'b0011), .in24(4'b0100),
    .in25(4'b0101), .in26(4'b0110), .in27(4'b0111), .in28(4'b1000), .in29(4'b1001), .in30(undriven),
    .out(_0), .sel(Y));  // open: in31, en
  Adder #(.width(5)) adder_1 (.a(Y), .b(5'b00001), .out(adder_1_out));  // open: cin, cout
  Adder #(.width(5)) adder_2 (.a(Y), .b(5'b00100), .out(adder_2_out));  // open: cin, cout
  Adder #(.width(5)) adder_3 (.a(Y), .b(5'b00111), .out(adder_3_out));  // open: cin, cout
  Multiplexer #(.select(5), .width(4)) multiplexer_2 (
    .in0(4'b0000), .in1(4'b0001), .in2(4'b0010), .in3(4'b0011), .in4(4'b0100), .in5(4'b0101), .in6(4'b0110),
    .in7(4'b0111), .in8(4'b1000), .in9(4'b1001), .in10(4'b0000), .in11(4'b0001), .in12(4'b0010),
    .in13(4'b0011), .in14(4'b0100), .in15(4'b0101), .in16(4'b0110), .in17(4'b0111), .in18(4'b1000),
    .in19(4'b1001), .in20(4'b0000), .in21(4'b0001), .in22(4'b0010), .in23(4'b0011), .in24(4'b0100),
    .in25(4'b0101), .in26(4'b0110), .in27(4'b0111), .in28(4'b1000), .in29(4'b1001), .in30(undriven_2),
    .out(_1), .sel(adder_1_out));  // open: in31, en
  Multiplexer #(.select(5), .width(4)) multiplexer_3 (
    .in0(4'b0000), .in1(4'b0001), .in2(4'b0010), .in3(4'b0011), .in4(4'b0100), .in5(4'b0101), .in6(4'b0110),
    .in7(4'b0111), .in8(4'b1000), .in9(4'b1001), .in10(4'b0000), .in11(4'b0001), .in12(4'b0010),
    .in13(4'b0011), .in14(4'b0100), .in15(4'b0101), .in16(4'b0110), .in17(4'b0111), .in18(4'b1000),
    .in19(4'b1001), .in20(4'b0000), .in21(4'b0001), .in22(4'b0010), .in23(4'b0011), .in24(4'b0100),
    .in25(4'b0101), .in26(4'b0110), .in27(4'b0111), .in28(4'b1000), .in29(4'b1001), .in30(undriven_3),
    .out(_4), .sel(adder_2_out));  // open: in31, en
  Multiplexer #(.select(5), .width(4)) multiplexer_4 (
    .in0(4'b0000), .in1(4'b0001), .in2(4'b0010), .in3(4'b0011), .in4(4'b0100), .in5(4'b0101), .in6(4'b0110),
    .in7(4'b0111), .in8(4'b1000), .in9(4'b1001), .in10(4'b0000), .in11(4'b0001), .in12(4'b0010),
    .in13(4'b0011), .in14(4'b0100), .in15(4'b0101), .in16(4'b0110), .in17(4'b0111), .in18(4'b1000),
    .in19(4'b1001), .in20(4'b0000), .in21(4'b0001), .in22(4'b0010), .in23(4'b0011), .in24(4'b0100),
    .in25(4'b0101), .in26(4'b0110), .in27(4'b0111), .in28(4'b1000), .in29(4'b1001), .in30(undriven_4),
    .out(_7), .sel(adder_3_out));  // open: in31, en
  Adder #(.width(5)) adder_4 (.a(Y), .b(5'b00010), .out(adder_4_out));  // open: cin, cout
  Adder #(.width(5)) adder_5 (.a(Y), .b(5'b00101), .out(adder_5_out));  // open: cin, cout
  Adder #(.width(5)) adder_6 (.a(Y), .b(5'b01000), .out(adder_6_out));  // open: cin, cout
  Multiplexer #(.select(5), .width(4)) multiplexer_5 (
    .in0(4'b0000), .in1(4'b0001), .in2(4'b0010), .in3(4'b0011), .in4(4'b0100), .in5(4'b0101), .in6(4'b0110),
    .in7(4'b0111), .in8(4'b1000), .in9(4'b1001), .in10(4'b0000), .in11(4'b0001), .in12(4'b0010),
    .in13(4'b0011), .in14(4'b0100), .in15(4'b0101), .in16(4'b0110), .in17(4'b0111), .in18(4'b1000),
    .in19(4'b1001), .in20(4'b0000), .in21(4'b0001), .in22(4'b0010), .in23(4'b0011), .in24(4'b0100),
    .in25(4'b0101), .in26(4'b0110), .in27(4'b0111), .in28(4'b1000), .in29(4'b1001), .in30(undriven_5),
    .out(_2), .sel(adder_4_out));  // open: in31, en
  Multiplexer #(.select(5), .width(4)) multiplexer_6 (
    .in0(4'b0000), .in1(4'b0001), .in2(4'b0010), .in3(4'b0011), .in4(4'b0100), .in5(4'b0101), .in6(4'b0110),
    .in7(4'b0111), .in8(4'b1000), .in9(4'b1001), .in10(4'b0000), .in11(4'b0001), .in12(4'b0010),
    .in13(4'b0011), .in14(4'b0100), .in15(4'b0101), .in16(4'b0110), .in17(4'b0111), .in18(4'b1000),
    .in19(4'b1001), .in20(4'b0000), .in21(4'b0001), .in22(4'b0010), .in23(4'b0011), .in24(4'b0100),
    .in25(4'b0101), .in26(4'b0110), .in27(4'b0111), .in28(4'b1000), .in29(4'b1001), .in30(undriven_6),
    .out(_5), .sel(adder_5_out));  // open: in31, en
  Multiplexer #(.select(5), .width(4)) multiplexer_7 (
    .in0(4'b0000), .in1(4'b0001), .in2(4'b0010), .in3(4'b0011), .in4(4'b0100), .in5(4'b0101), .in6(4'b0110),
    .in7(4'b0111), .in8(4'b1000), .in9(4'b1001), .in10(4'b0000), .in11(4'b0001), .in12(4'b0010),
    .in13(4'b0011), .in14(4'b0100), .in15(4'b0101), .in16(4'b0110), .in17(4'b0111), .in18(4'b1000),
    .in19(4'b1001), .in20(4'b0000), .in21(4'b0001), .in22(4'b0010), .in23(4'b0011), .in24(4'b0100),
    .in25(4'b0101), .in26(4'b0110), .in27(4'b0111), .in28(4'b1000), .in29(4'b1001), .in30(undriven_7),
    .out(_8), .sel(adder_6_out));  // open: in31, en
  Multiplexer #(.select(5), .width(4)) multiplexer_8 (
    .in0(4'b0000), .in1(4'b0001), .in2(4'b0010), .in3(4'b0011), .in4(4'b0100), .in5(4'b0101), .in6(4'b0110),
    .in7(4'b0111), .in8(4'b1000), .in9(4'b1001), .in10(4'b0000), .in11(4'b0001), .in12(4'b0010),
    .in13(4'b0011), .in14(4'b0100), .in15(4'b0101), .in16(4'b0110), .in17(4'b0111), .in18(4'b1000),
    .in19(4'b1001), .in20(4'b0000), .in21(4'b0001), .in22(4'b0010), .in23(4'b0011), .in24(4'b0100),
    .in25(4'b0101), .in26(4'b0110), .in27(4'b0111), .in28(4'b1000), .in29(4'b1001), .in30(undriven_8),
    .out(_3), .sel(adder_7_out));  // open: in31, en
  Adder #(.width(5)) adder_7 (.a(Y), .b(5'b00011), .out(adder_7_out));  // open: cin, cout
  Multiplexer #(.select(5), .width(4)) multiplexer_9 (
    .in0(4'b0000), .in1(4'b0001), .in2(4'b0010), .in3(4'b0011), .in4(4'b0100), .in5(4'b0101), .in6(4'b0110),
    .in7(4'b0111), .in8(4'b1000), .in9(4'b1001), .in10(4'b0000), .in11(4'b0001), .in12(4'b0010),
    .in13(4'b0011), .in14(4'b0100), .in15(4'b0101), .in16(4'b0110), .in17(4'b0111), .in18(4'b1000),
    .in19(4'b1001), .in20(4'b0000), .in21(4'b0001), .in22(4'b0010), .in23(4'b0011), .in24(4'b0100),
    .in25(4'b0101), .in26(4'b0110), .in27(4'b0111), .in28(4'b1000), .in29(4'b1001), .in30(undriven_9),
    .out(_6), .sel(adder_8_out));  // open: in31, en
  Adder #(.width(5)) adder_8 (.a(Y), .b(5'b00110), .out(adder_8_out));  // open: cin, cout
  Multiplexer #(.select(5), .width(4)) multiplexer_10 (
    .in0(4'b0000), .in1(4'b0001), .in2(4'b0010), .in3(4'b0011), .in4(4'b0100), .in5(4'b0101), .in6(4'b0110),
    .in7(4'b0111), .in8(4'b1000), .in9(4'b1001), .in10(4'b0000), .in11(4'b0001), .in12(4'b0010),
    .in13(4'b0011), .in14(4'b0100), .in15(4'b0101), .in16(4'b0110), .in17(4'b0111), .in18(4'b1000),
    .in19(4'b1001), .in20(4'b0000), .in21(4'b0001), .in22(4'b0010), .in23(4'b0011), .in24(4'b0100),
    .in25(4'b0101), .in26(4'b0110), .in27(4'b0111), .in28(4'b1000), .in29(4'b1001), .in30(undriven_10),
    .out(_9), .sel(adder_9_out));  // open: in31, en
  Adder #(.width(5)) adder_9 (.a(Y), .b(5'b01001), .out(adder_9_out));  // open: cin, cout
endmodule

module rom_check_counter (
  output [9:0] ADDR,
  output [3:0] ADDR_LOW_4
);

  wire and_1_out, clock_1_out, not_1_out, not_2_out, not_3_out, not_4_out, not_5_out, not_6_out;
  wire [8:0] adder_1_out;

  Clock clock_1 (.out(clock_1_out));
  Adder #(.width(9)) adder_1 (.a(ADDR[8:0]), .b(9'h1), .out(adder_1_out));  // open: cin, cout
  Register #(.width(9)) register_1 (.D(adder_1_out), .Q(ADDR[8:0]), .clk(clock_1_out), .clr(and_1_out));  // open: en
  not not_1 (not_1_out, ADDR[2]);
  not not_2 (not_2_out, ADDR[3]);
  not not_3 (not_3_out, ADDR[7]);
  not not_4 (not_4_out, ADDR[6]);
  and and_1 (and_1_out, ADDR[8], not_3_out, not_4_out, ADDR[5], ADDR[4], not_2_out, not_1_out, not_5_out, not_6_out);
  not not_5 (not_5_out, ADDR[1]);
  not not_6 (not_6_out, ADDR[0]);

  assign ADDR[9] = 1'b0;
  assign ADDR_LOW_4 = ADDR[3:0];
endmodule

module block_addr_gen (
  input  [5:0] BLOCK_NUM,
  output [3:0] OUT_ADDR_LOW_4,
  output [9:0] OUT_ADDR
);

  wire clock_1_out;
  wire [3:0] adder_1_out;

  Adder #(.width(4)) adder_1 (.a(OUT_ADDR[3:0]), .b(4'b0001), .out(adder_1_out));  // open: cin, cout
  Clock clock_1 (.out(clock_1_out));
  Register #(.width(4)) register_1 (.D(adder_1_out), .Q(OUT_ADDR[3:0]), .clk(clock_1_out));  // open: en, clr

  assign OUT_ADDR[9:4] = BLOCK_NUM;
  assign OUT_ADDR_LOW_4 = OUT_ADDR[3:0];
endmodule

module flip_logic (
  input  [5:0] BLOCK_NUM,
  input  FLIP,
  output [5:0] OUT
);

  wire adder_2_out, clock_1_out, comparator_1_eq, comparator_2_eq, comparator_3_eq, comparator_4_eq,
       comparator_5_eq, comparator_6_eq, multiplexer_2_out;
  wire [0:0] register_2_q;
  wire [1:0] adder_1_out, multiplexer_1_out, multiplexer_3_out, or_1_out, register_1_q;

  Clock clock_1 (.out(clock_1_out));
  Adder #(.width(2)) adder_1 (.a(register_1_q), .b(2'b01), .out(adder_1_out));  // open: cin, cout
  Adder #(.width(1)) adder_2 (.a(register_2_q[0]), .b(1'b1), .out(adder_2_out));  // open: cin, cout
  Multiplexer #(.width(2), .enable("false")) multiplexer_1 (
    .in0(register_1_q), .in1(adder_1_out), .out(multiplexer_1_out), .sel(FLIP));
  Multiplexer #(.enable("false")) multiplexer_2 (
    .in0(register_2_q[0]), .in1(adder_2_out), .out(multiplexer_2_out), .sel(FLIP));
  Register #(.width(2)) register_1 (
    .D(multiplexer_1_out), .en(or_1_out[0]), .Q(register_1_q), .clk(clock_1_out));  // open: clr
  Register #(.width(1)) register_2 (
    .D(multiplexer_2_out), .en(or_1_out[1]), .Q(register_2_q[0]), .clk(clock_1_out));  // open: clr
  Comparator #(.width(6), .mode("unsigned")) comparator_1 (
    .a(BLOCK_NUM), .b({6{1'b0}}), .eq(comparator_1_eq));  // open: gt, lt
  Comparator #(.width(6), .mode("unsigned")) comparator_2 (
    .a(BLOCK_NUM), .b(6'b000100), .eq(comparator_2_eq));  // open: gt, lt
  Comparator #(.width(6), .mode("unsigned")) comparator_3 (
    .a(BLOCK_NUM), .b(6'b001000), .eq(comparator_3_eq));  // open: gt, lt
  Comparator #(.width(6), .mode("unsigned")) comparator_4 (
    .a(BLOCK_NUM), .b(6'b001101), .eq(comparator_4_eq));  // open: gt, lt
  Comparator #(.width(6), .mode("unsigned")) comparator_5 (
    .a(BLOCK_NUM), .b(6'b001111), .eq(comparator_5_eq));  // open: gt, lt
  Comparator #(.width(6), .mode("unsigned")) comparator_6 (
    .a(BLOCK_NUM), .b(6'b010001), .eq(comparator_6_eq));  // open: gt, lt
  or or_1 (or_1_out[0], comparator_1_eq, comparator_2_eq, comparator_3_eq);
  or or_2 (or_1_out[1], comparator_4_eq, comparator_5_eq, comparator_6_eq);
  Multiplexer #(.select(2), .width(2)) multiplexer_3 (
    .in0(2'b00), .in1(register_1_q), .in2({1'b0, register_2_q[0]}), .in3(2'b00), .out(multiplexer_3_out),
    .sel(or_1_out));  // open: en
  Adder #(.width(6)) adder_3 (.a(BLOCK_NUM), .b({4'b0000, multiplexer_3_out}), .out(OUT));  // open: cin, cout

  // Notes on the sheet:
  //   4 POSITIONS
  //   2 POSITIONS
endmodule

module auto_fall (
  input  [7:0] SPEED,
  input  FALL,
  input  RESET,
  output [4:0] OUT
);

  wire clock_1_out, comparator_1_lt, comparator_2_eq, or_1_out;
  wire [0:0] comparator_1_eq;
  wire [4:0] adder_2_out;
  wire [7:0] adder_1_out, register_1_q;

  Clock clock_1 (.out(clock_1_out));
  Adder adder_1 (.a(register_1_q), .b(8'h1), .out(adder_1_out));  // open: cin, cout
  Comparator #(.mode("unsigned")) comparator_1 (
    .a(SPEED), .b(register_1_q), .eq(comparator_1_eq[0]), .lt(comparator_1_lt));  // open: gt
  Register register_1 (.D(adder_1_out), .Q(register_1_q), .clk(clock_1_out), .clr(comparator_1_lt));  // open: en
  Adder #(.width(5)) adder_2 (.a({4'b0000, comparator_1_eq[0]}), .b(OUT), .out(adder_2_out));  // open: cin, cout
  Register #(.width(5)) register_2 (.D(adder_2_out), .en(FALL), .Q(OUT), .clk(clock_1_out), .clr(or_1_out));
  or or_1 (or_1_out, RESET, comparator_2_eq);
  Comparator #(.width(5), .mode("unsigned")) comparator_2 (
    .a(OUT), .b(5'b10101), .eq(comparator_2_eq));  // open: gt, lt
endmodule

module block_ind_2_block_num (
  input  [2:0] BLOCK_IND,
  output [5:0] BLOCK_NUM
);

  Multiplexer #(.select(3), .width(6)) multiplexer_1 (
    .in0({6{1'b0}}), .in1(6'b000100), .in2(6'b001000), .in3(6'b001100), .in4(6'b001101), .in5(6'b001111),
    .in6(6'b010001), .in7({6{1'b0}}), .out(BLOCK_NUM), .sel(BLOCK_IND));  // open: en
endmodule

module gen_rand_block (
  input  NEXT,
  output [5:0] BLOCK_NUM
);

  wire clock_1_out, clock_2_out;
  wire [2:0] register_1_q, xor_1_out;
  wire [7:0] random_1_out, random_2_out;
  wire [7:3] xor_1_out_2;

  Clock #(.highDuration(3), .lowDuration(3)) clock_1 (.out(clock_1_out));
  Clock clock_2 (.out(clock_2_out));
  Random random_1 (.clk(clock_2_out), .out(random_1_out));  // open: next, clr
  Random random_2 (.clk(clock_1_out), .out(random_2_out));  // open: next, clr
  Register #(.width(3)) register_1 (.D(xor_1_out), .en(NEXT), .Q(register_1_q), .clk(clock_2_out));  // open: clr
  assign {xor_1_out_2, xor_1_out} = random_1_out ^ random_2_out;  // XOR_Gate xor_1, 8 bits wide
  block_ind_2_block_num block_ind_2_block_num_1 (.BLOCK_NUM(BLOCK_NUM), .BLOCK_IND(register_1_q));
endmodule

module collision_detect (
  input  [19:0] BLOCK,
  input  [19:0] MAP,
  input  ACK,
  output COLLISION
);

  wire clock_1_out, comparator_1_eq, comparator_2_gt, d_ff_1_q;
  wire [19:0] and_1_out, multiplexer_1_out, shifter_1_out;

  Shifter #(.width(20)) shifter_1 (.in(MAP), .\dist (5'b00001), .out(shifter_1_out));
  Multiplexer #(.width(20)) multiplexer_1 (
    .in0(shifter_1_out), .in1(20'h1), .out(multiplexer_1_out), .sel(comparator_1_eq));  // open: en
  Comparator #(.width(20), .mode("unsigned")) comparator_1 (
    .a(MAP), .b({20{1'b0}}), .eq(comparator_1_eq));  // open: gt, lt
  assign and_1_out = BLOCK & multiplexer_1_out;  // AND_Gate and_1, 20 bits wide
  Clock clock_1 (.out(clock_1_out));
  Comparator #(.width(20), .mode("unsigned")) comparator_2 (
    .a(and_1_out), .b({20{1'b0}}), .gt(comparator_2_gt));  // open: eq, lt
  D_Flip_Flop d_ff_1 (.clk(clock_1_out), .D(ACK), .Q(d_ff_1_q));  // open: Qn, preset, en, reset
  S_R_Flip_Flop s_r_ff_1 (
    .S(comparator_2_gt), .clk(clock_1_out), .R(d_ff_1_q), .Q(COLLISION));  // open: Qn, preset, reset, en
endmodule

module row_detect (
  input  [19:0] _0,
  input  [19:0] _1,
  input  [19:0] _2,
  input  [4:0] ROW,
  input  [19:0] _3,
  input  [19:0] _4,
  input  [19:0] _5,
  input  [19:0] _6,
  input  [19:0] _7,
  input  [19:0] _8,
  input  [19:0] _9,
  output HIT,
  output [19:0] out_13,
  output [19:0] out_14,
  output [19:0] out_15,
  output [19:0] out_16,
  output [19:0] out_17,
  output [19:0] out_18,
  output [19:0] out_19,
  output [19:0] out_20,
  output [19:0] out_21,
  output [19:0] out_22
);

  wire or_1_out, or_12_out, or_13_out, or_14_out, or_15_out, or_16_out, or_17_out, or_18_out, or_19_out,
       or_20_out;
  wire [4:0] adder_1_out;
  wire [19:0] and_1_out, and_2_out, and_3_out, and_4_out, and_5_out, and_6_out, and_7_out, and_8_out,
       and_9_out, and_10_out, and_11_out, and_12_out, and_13_out, and_14_out, and_15_out, and_16_out,
       and_17_out, and_18_out, and_19_out, and_20_out, multiplexer_1_out, multiplexer_2_out, or_2_out,
       or_3_out, or_4_out, or_5_out, or_6_out, or_7_out, or_8_out, or_9_out, or_10_out, or_11_out,
       shifter_1_out, shifter_2_out, shifter_3_out, shifter_4_out, shifter_5_out, shifter_6_out,
       shifter_7_out, shifter_8_out, shifter_9_out, shifter_10_out, shifter_11_out, shifter_12_out,
       shifter_13_out, shifter_14_out, shifter_15_out, shifter_16_out, shifter_17_out, shifter_18_out,
       shifter_19_out, shifter_20_out;

  Multiplexer #(.select(5), .width(20)) multiplexer_1 (
    .in0(20'h1), .in1(20'h2), .in2(20'h4), .in3(20'h8), .in4(20'h10), .in5(20'h20), .in6(20'h40),
    .in7(20'h80), .in8(20'h100), .in9(20'h200), .in10(20'h400), .in11(20'h800), .in12(20'h1000),
    .in13(20'h2000), .in14(20'h4000), .in15(20'h8000), .in16(20'h10000), .in17(20'h20000), .in18(20'h40000),
    .in19(20'h80000), .in20(20'h1), .in21(20'h1), .in22(20'h1), .in23(20'h1), .in24(20'h1), .in25(20'h1),
    .in26(20'h1), .in27(20'h1), .in28(20'h1), .in29(20'h1), .in30(20'h1), .in31(20'h1),
    .out(multiplexer_1_out), .sel(ROW));  // open: en
  Adder #(.width(5)) adder_1 (.a(ROW), .b(5'b00001), .out(adder_1_out));  // open: cin, cout
  Shifter #(.width(20), .shift("lr")) shifter_1 (.in(_0), .\dist (adder_1_out), .out(shifter_1_out));
  Shifter #(.width(20), .shift("lr")) shifter_2 (.in(_1), .\dist (adder_1_out), .out(shifter_2_out));
  Shifter #(.width(20), .shift("lr")) shifter_3 (.in(_2), .\dist (adder_1_out), .out(shifter_3_out));
  Shifter #(.width(20), .shift("lr")) shifter_4 (.in(_3), .\dist (adder_1_out), .out(shifter_4_out));
  Shifter #(.width(20), .shift("lr")) shifter_5 (.in(_4), .\dist (adder_1_out), .out(shifter_5_out));
  Shifter #(.width(20), .shift("lr")) shifter_6 (.in(_5), .\dist (adder_1_out), .out(shifter_6_out));
  Shifter #(.width(20), .shift("lr")) shifter_7 (.in(_6), .\dist (adder_1_out), .out(shifter_7_out));
  Shifter #(.width(20), .shift("lr")) shifter_8 (.in(_7), .\dist (adder_1_out), .out(shifter_8_out));
  Shifter #(.width(20), .shift("lr")) shifter_9 (.in(_8), .\dist (adder_1_out), .out(shifter_9_out));
  Shifter #(.width(20), .shift("lr")) shifter_10 (.in(_9), .\dist (adder_1_out), .out(shifter_10_out));
  Shifter #(.width(20)) shifter_11 (.in(shifter_1_out), .\dist (ROW), .out(shifter_11_out));
  Shifter #(.width(20)) shifter_12 (.in(shifter_2_out), .\dist (ROW), .out(shifter_12_out));
  Shifter #(.width(20)) shifter_13 (.in(shifter_3_out), .\dist (ROW), .out(shifter_13_out));
  Shifter #(.width(20)) shifter_14 (.in(shifter_4_out), .\dist (ROW), .out(shifter_14_out));
  Shifter #(.width(20)) shifter_15 (.in(shifter_5_out), .\dist (ROW), .out(shifter_15_out));
  Shifter #(.width(20)) shifter_16 (.in(shifter_6_out), .\dist (ROW), .out(shifter_16_out));
  Shifter #(.width(20)) shifter_17 (.in(shifter_7_out), .\dist (ROW), .out(shifter_17_out));
  Shifter #(.width(20)) shifter_18 (.in(shifter_8_out), .\dist (ROW), .out(shifter_18_out));
  Shifter #(.width(20)) shifter_19 (.in(shifter_9_out), .\dist (ROW), .out(shifter_19_out));
  Shifter #(.width(20)) shifter_20 (.in(shifter_10_out), .\dist (ROW), .out(shifter_20_out));
  Multiplexer #(.select(5), .width(20)) multiplexer_2 (
    .in0({20{1'b0}}), .in1(20'h1), .in2(20'h3), .in3(20'h7), .in4(20'hf), .in5(20'h1f), .in6(20'h3f),
    .in7(20'h7f), .in8(20'hff), .in9(20'h1ff), .in10(20'h3ff), .in11(20'h7ff), .in12(20'hfff),
    .in13(20'h1fff), .in14(20'h3fff), .in15(20'h7fff), .in16(20'hffff), .in17(20'h1ffff), .in18(20'h3ffff),
    .in19(20'h7ffff), .in20({20{1'b1}}), .in21({20{1'b1}}), .in22({20{1'b1}}), .in23({20{1'b1}}),
    .in24({20{1'b1}}), .in25({20{1'b1}}), .in26({20{1'b1}}), .in27({20{1'b1}}), .in28({20{1'b1}}),
    .in29({20{1'b1}}), .in30({20{1'b1}}), .in31({20{1'b1}}), .out(multiplexer_2_out), .sel(ROW));  // open: en
  assign and_1_out = multiplexer_1_out & _0;  // AND_Gate and_1, 20 bits wide
  assign and_2_out = multiplexer_1_out & _1;  // AND_Gate and_2, 20 bits wide
  assign and_3_out = multiplexer_1_out & _2;  // AND_Gate and_3, 20 bits wide
  assign and_4_out = multiplexer_1_out & _3;  // AND_Gate and_4, 20 bits wide
  assign and_5_out = multiplexer_1_out & _4;  // AND_Gate and_5, 20 bits wide
  assign and_6_out = multiplexer_1_out & _5;  // AND_Gate and_6, 20 bits wide
  assign and_7_out = multiplexer_1_out & _6;  // AND_Gate and_7, 20 bits wide
  assign and_8_out = multiplexer_1_out & _7;  // AND_Gate and_8, 20 bits wide
  assign and_9_out = multiplexer_1_out & _8;  // AND_Gate and_9, 20 bits wide
  assign and_10_out = multiplexer_1_out & _9;  // AND_Gate and_10, 20 bits wide
  assign and_11_out = _0 & multiplexer_2_out;  // AND_Gate and_11, 20 bits wide
  assign and_12_out = _1 & multiplexer_2_out;  // AND_Gate and_12, 20 bits wide
  assign and_13_out = _2 & multiplexer_2_out;  // AND_Gate and_13, 20 bits wide
  assign and_14_out = _3 & multiplexer_2_out;  // AND_Gate and_14, 20 bits wide
  assign and_15_out = _4 & multiplexer_2_out;  // AND_Gate and_15, 20 bits wide
  assign and_16_out = _5 & multiplexer_2_out;  // AND_Gate and_16, 20 bits wide
  assign and_17_out = _6 & multiplexer_2_out;  // AND_Gate and_17, 20 bits wide
  assign and_18_out = _7 & multiplexer_2_out;  // AND_Gate and_18, 20 bits wide
  assign and_19_out = _8 & multiplexer_2_out;  // AND_Gate and_19, 20 bits wide
  assign and_20_out = _9 & multiplexer_2_out;  // AND_Gate and_20, 20 bits wide
  or or_1 (or_1_out, and_1_out[19], and_1_out[18], and_1_out[17], and_1_out[16], and_1_out[15], and_1_out[14], and_1_out[13], and_1_out[12], and_1_out[11], and_1_out[10], and_1_out[9], and_1_out[8], and_1_out[7], and_1_out[6], and_1_out[5], and_1_out[4], and_1_out[3], and_1_out[2], and_1_out[1], and_1_out[0]);
  assign or_2_out = shifter_11_out | and_11_out;  // OR_Gate or_2, 20 bits wide
  assign or_3_out = shifter_12_out | and_12_out;  // OR_Gate or_3, 20 bits wide
  assign or_4_out = shifter_13_out | and_13_out;  // OR_Gate or_4, 20 bits wide
  assign or_5_out = shifter_14_out | and_14_out;  // OR_Gate or_5, 20 bits wide
  assign or_6_out = shifter_15_out | and_15_out;  // OR_Gate or_6, 20 bits wide
  assign or_7_out = shifter_16_out | and_16_out;  // OR_Gate or_7, 20 bits wide
  assign or_8_out = shifter_17_out | and_17_out;  // OR_Gate or_8, 20 bits wide
  assign or_9_out = shifter_18_out | and_18_out;  // OR_Gate or_9, 20 bits wide
  assign or_10_out = shifter_19_out | and_19_out;  // OR_Gate or_10, 20 bits wide
  assign or_11_out = shifter_20_out | and_20_out;  // OR_Gate or_11, 20 bits wide
  Multiplexer #(.width(20), .enable("false")) multiplexer_3 (.in0(_0), .in1(or_2_out), .out(out_13), .sel(HIT));
  Multiplexer #(.width(20), .enable("false")) multiplexer_4 (.in0(_1), .in1(or_3_out), .out(out_14), .sel(HIT));
  Multiplexer #(.width(20), .enable("false")) multiplexer_5 (.in0(_2), .in1(or_4_out), .out(out_15), .sel(HIT));
  Multiplexer #(.width(20), .enable("false")) multiplexer_6 (.in0(_3), .in1(or_5_out), .out(out_16), .sel(HIT));
  Multiplexer #(.width(20), .enable("false")) multiplexer_7 (.in0(_4), .in1(or_6_out), .out(out_17), .sel(HIT));
  Multiplexer #(.width(20), .enable("false")) multiplexer_8 (.in0(_5), .in1(or_7_out), .out(out_18), .sel(HIT));
  Multiplexer #(.width(20), .enable("false")) multiplexer_9 (.in0(_6), .in1(or_8_out), .out(out_19), .sel(HIT));
  Multiplexer #(.width(20), .enable("false")) multiplexer_10 (.in0(_7), .in1(or_9_out), .out(out_20), .sel(HIT));
  Multiplexer #(.width(20), .enable("false")) multiplexer_11 (.in0(_8), .in1(or_10_out), .out(out_21), .sel(HIT));
  Multiplexer #(.width(20), .enable("false")) multiplexer_12 (.in0(_9), .in1(or_11_out), .out(out_22), .sel(HIT));
  or or_12 (or_12_out, and_2_out[19], and_2_out[18], and_2_out[17], and_2_out[16], and_2_out[15], and_2_out[14], and_2_out[13], and_2_out[12], and_2_out[11], and_2_out[10], and_2_out[9], and_2_out[8], and_2_out[7], and_2_out[6], and_2_out[5], and_2_out[4], and_2_out[3], and_2_out[2], and_2_out[1], and_2_out[0]);
  or or_13 (or_13_out, and_3_out[19], and_3_out[18], and_3_out[17], and_3_out[16], and_3_out[15], and_3_out[14], and_3_out[13], and_3_out[12], and_3_out[11], and_3_out[10], and_3_out[9], and_3_out[8], and_3_out[7], and_3_out[6], and_3_out[5], and_3_out[4], and_3_out[3], and_3_out[2], and_3_out[1], and_3_out[0]);
  or or_14 (or_14_out, and_4_out[19], and_4_out[18], and_4_out[17], and_4_out[16], and_4_out[15], and_4_out[14], and_4_out[13], and_4_out[12], and_4_out[11], and_4_out[10], and_4_out[9], and_4_out[8], and_4_out[7], and_4_out[6], and_4_out[5], and_4_out[4], and_4_out[3], and_4_out[2], and_4_out[1], and_4_out[0]);
  or or_15 (or_15_out, and_5_out[19], and_5_out[18], and_5_out[17], and_5_out[16], and_5_out[15], and_5_out[14], and_5_out[13], and_5_out[12], and_5_out[11], and_5_out[10], and_5_out[9], and_5_out[8], and_5_out[7], and_5_out[6], and_5_out[5], and_5_out[4], and_5_out[3], and_5_out[2], and_5_out[1], and_5_out[0]);
  or or_16 (or_16_out, and_6_out[19], and_6_out[18], and_6_out[17], and_6_out[16], and_6_out[15], and_6_out[14], and_6_out[13], and_6_out[12], and_6_out[11], and_6_out[10], and_6_out[9], and_6_out[8], and_6_out[7], and_6_out[6], and_6_out[5], and_6_out[4], and_6_out[3], and_6_out[2], and_6_out[1], and_6_out[0]);
  or or_17 (or_17_out, and_7_out[19], and_7_out[18], and_7_out[17], and_7_out[16], and_7_out[15], and_7_out[14], and_7_out[13], and_7_out[12], and_7_out[11], and_7_out[10], and_7_out[9], and_7_out[8], and_7_out[7], and_7_out[6], and_7_out[5], and_7_out[4], and_7_out[3], and_7_out[2], and_7_out[1], and_7_out[0]);
  or or_18 (or_18_out, and_8_out[19], and_8_out[18], and_8_out[17], and_8_out[16], and_8_out[15], and_8_out[14], and_8_out[13], and_8_out[12], and_8_out[11], and_8_out[10], and_8_out[9], and_8_out[8], and_8_out[7], and_8_out[6], and_8_out[5], and_8_out[4], and_8_out[3], and_8_out[2], and_8_out[1], and_8_out[0]);
  or or_19 (or_19_out, and_9_out[19], and_9_out[18], and_9_out[17], and_9_out[16], and_9_out[15], and_9_out[14], and_9_out[13], and_9_out[12], and_9_out[11], and_9_out[10], and_9_out[9], and_9_out[8], and_9_out[7], and_9_out[6], and_9_out[5], and_9_out[4], and_9_out[3], and_9_out[2], and_9_out[1], and_9_out[0]);
  or or_20 (or_20_out, and_10_out[19], and_10_out[18], and_10_out[17], and_10_out[16], and_10_out[15], and_10_out[14], and_10_out[13], and_10_out[12], and_10_out[11], and_10_out[10], and_10_out[9], and_10_out[8], and_10_out[7], and_10_out[6], and_10_out[5], and_10_out[4], and_10_out[3], and_10_out[2], and_10_out[1], and_10_out[0]);
  and and_21 (HIT, or_1_out, or_12_out, or_13_out, or_14_out, or_15_out, or_16_out, or_17_out, or_18_out, or_19_out, or_20_out);

  // Other names for the same wires on the sheet: IN0[19:0] = _0; IN1[19:0] = _1; IN2[19:0] = _2; IN3[19:0] = _3;
  //   IN4[19:0] = _4; IN5[19:0] = _5; IN6[19:0] = _6; IN7[19:0] = _7; IN8[19:0] = _8; IN9[19:0] = _9
endmodule
